# Fritzing sketch dfu_update (saved by Fritzing 1.0.4)
breadboards: 2

parts:
  Micro_uSB = Adafruit Micro USB Breakout [part_number="Adafruit #1833"]
  Power_Supply = Breadboard Power Supply Board SMD
  POWER = Momentary Switch [package=ksa_sealed_tac_switch]
  DFU_Mode = SWITCH_SPDT [package=kps-1290]
  RN-52_Breakout3 = RN-52 Breakout

nets (from the schematic view):
  GND: Micro_uSB.GND, Power_Supply.GND, RN-52_Breakout3.GND
  USB D+: Micro_uSB.D+, RN-52_Breakout3.USBD+
  USB D-: Micro_uSB.D-, RN-52_Breakout3.USBD-
  3.3 V: Power_Supply.VIN, POWER.2, DFU_Mode.P, RN-52_Breakout3.3.3V
  PWREN: POWER.4, RN-52_Breakout3.PWREN
  GPIO3: DFU_Mode.O, RN-52_Breakout3.GPIO3

custom parts:
  Adafruit Micro USB Breakout: Simple but effective - this breakout board has a USB Micro-B connector, with all 5 pins broken out. Great for pairing with a microcontroller with USB support, or adding USB 5V power to a project. We use a micro-AB connector with through-hole shielding pads for an excellent strong connection - it won't rip off by accident! Comes with one fully assembled and tested micro B breakout PCB and a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
  RN-52 Breakout: RN-52 Breakout with smaller schematic footprint
